# Fritzing sketch Sketch (saved by Fritzing 0.9.9b)
breadboards: 1

parts:
  Part1 = Arduino Uno (Rev3) - ICSP [part_number="Arduino Uno"]
  Part2 = Thumb Joystick [part_number=Joystick]
  J2 = Basic Servo [part_number="Y-Axis (Vertical) Servo"]
  J1 = Basic Servo [part_number="X-Axis (Horizontal) Servo"]

nets:
  N1: Part1.A0, Part2.HORZ
  N2: Part1.A1, Part2.VERT
  VCC: Part1.5V, Part2.VCC, J2.vcc, J1.vcc
  N3: Part1.D3_PWM, J2.pulse
  N4: Part1.D4, J1.pulse
  GND: Part1.GND, Part2.GND, J2.gnd, J1.gnd
